# Fritzing sketch led_duell (saved by Fritzing 0.9.3b)
breadboards: 2

parts:
  LED10 = smd LED [color="Red (633nm)" package="0805 [SMD]"]
  LED16 = smd LED [color="Red (633nm)" package="0805 [SMD]"]
  LED8 = smd LED [color="Red (633nm)" package="0805 [SMD]"]
  LED21 = smd LED [color="Red (633nm)" package="0805 [SMD]"]
  LED9 = smd LED [color="Red (633nm)" package="0805 [SMD]"]
  LED17 = smd LED [color="Red (633nm)" package="0805 [SMD]"]
  LED7 = smd LED [color="Red (633nm)" package="0805 [SMD]"]
  LED5 = smd LED [color="Red (633nm)" package="0805 [SMD]"]
  LED1 = smd LED [color="Red (633nm)" package="0805 [SMD]"]
  LED14 = smd LED [color="Red (633nm)" package="0805 [SMD]"]
  LED3 = smd LED [color="Red (633nm)" package="0805 [SMD]"]
  LED12 = smd LED [color="Red (633nm)" package="0805 [SMD]"]
  LED19 = smd LED [color="Red (633nm)" package="0805 [SMD]"]
  LED2 = smd LED [color="Red (633nm)" package="0805 [SMD]"]
  LED15 = smd LED [color="Red (633nm)" package="0805 [SMD]"]
  LED11 = smd LED [color="Red (633nm)" package="0805 [SMD]"]
  LED4 = smd LED [color="Red (633nm)" package="0805 [SMD]"]
  LED13 = smd LED [color="Red (633nm)" package="0805 [SMD]"]
  LED18 = smd LED [color="Red (633nm)" package="0805 [SMD]"]
  LED20 = smd LED [color="Red (633nm)" package="0805 [SMD]"]
  LED6 = smd LED [color="Red (633nm)" package="0805 [SMD]"]
  R1 = Resistor [tolerance=±5% resistance=220 package=THT]
  R2 = Resistor [tolerance=±5% resistance=220 package=THT]
  R3 = Resistor [tolerance=±5% resistance=220 package=THT]
  R4 = Resistor [tolerance=±5% resistance=220 package=THT]
  R5 = Resistor [tolerance=±5% resistance=220 package=THT]
  R6 = Resistor [tolerance=±5% resistance=220 package=THT]
  R7 = Resistor [tolerance=±5% resistance=220 package=THT]
  R8 = Resistor [tolerance=±5% resistance=220 package=THT]
  R9 = Resistor [tolerance=±5% resistance=220 package=THT]
  R10 = Resistor [tolerance=±5% resistance=220 package=THT]
  R11 = Resistor [tolerance=±5% resistance=220 package=THT]
  R12 = Resistor [tolerance=±5% resistance=220 package=THT]
  R13 = Resistor [tolerance=±5% resistance=220 package=THT]
  R14 = Resistor [tolerance=±5% resistance=220 package=THT]
  R15 = Resistor [tolerance=±5% resistance=220 package=THT]
  R16 = Resistor [tolerance=±5% resistance=220 package=THT]
  R17 = Resistor [tolerance=±5% resistance=220 package=THT]
  R18 = Resistor [tolerance=±5% resistance=220 package=THT]
  R19 = Resistor [tolerance=±5% resistance=220 package=THT]
  R20 = Resistor [tolerance=±5% resistance=220 package=THT]
  R21 = Resistor [tolerance=±5% resistance=220 package=THT]
  Mod1 = Raspberry Pi Pico
  S1 = Pushbutton [package="[THT]"]
  S2 = Pushbutton [package="[THT]"]

nets:
  N1: LED10.cathode, LED16.cathode, LED8.cathode, LED21.cathode, LED9.cathode, LED17.cathode, LED7.cathode, LED5.cathode, LED1.cathode, LED14.cathode, LED3.cathode, LED12.cathode, LED19.cathode, LED2.cathode, LED15.cathode, LED11.cathode, LED4.cathode, LED13.cathode, LED18.cathode, LED20.cathode, LED6.cathode, Mod1.pin_3, Mod1.pin_8, Mod1.pin_13, Mod1.pin_18, Mod1.pin_23, Mod1.pin_28, Mod1.pin_32, Mod1.pin_33, Mod1.pin_34, Mod1.pin_38, S1.Pin_1, S1.Pin_2, S1.Pin_3, S1.Pin_4, S2.Pin_1, S2.Pin_2, S2.Pin_3, S2.Pin_4
  N2: LED10.anode, R12.Pin_0
  N3: LED16.anode, R6.Pin_0
  N4: LED8.anode, R14.Pin_0
  N5: LED21.anode, R1.Pin_0
  N6: LED9.anode, R13.Pin_0
  N7: LED17.anode, R5.Pin_0
  N8: LED7.anode, R15.Pin_0
  N9: LED5.anode, R17.Pin_0
  N10: LED1.anode, R21.Pin_0
  N11: LED14.anode, R8.Pin_0
  N12: LED3.anode, R19.Pin_0
  N13: LED12.anode, R10.Pin_0
  N14: LED19.anode, R3.Pin_0
  N15: LED2.anode, R20.Pin_0
  N16: LED15.anode, R7.Pin_0
  N17: LED11.anode, R11.Pin_0
  N18: LED4.anode, R18.Pin_0
  N19: LED13.anode, R9.Pin_0
  N20: LED18.anode, R4.Pin_0
  N21: LED20.anode, R2.Pin_0
  N22: LED6.anode, R16.Pin_0
  N23: R1.Pin_1, Mod1.pin_1
  N24: R2.Pin_1, Mod1.pin_2
  N25: R3.Pin_1, Mod1.pin_4
  N26: R4.Pin_1, Mod1.pin_5
  N27: R5.Pin_1, Mod1.pin_6
  N28: R6.Pin_1, Mod1.pin_7
  N29: R7.Pin_1, Mod1.pin_9
  N30: R8.Pin_1, Mod1.pin_10
  N31: R9.Pin_1, Mod1.pin_11
  N32: R10.Pin_1, Mod1.pin_12
  N33: R11.Pin_1, Mod1.pin_14
  N34: R12.Pin_1, Mod1.pin_15
  N35: R13.Pin_1, Mod1.pin_16
  N36: R14.Pin_1, Mod1.pin_17
  N37: R15.Pin_1, Mod1.pin_19
  N38: R16.Pin_1, Mod1.pin_20
  N39: R17.Pin_1, Mod1.pin_21
  N40: R18.Pin_1, Mod1.pin_22
  N41: R19.Pin_1, Mod1.pin_24
  N42: R20.Pin_1, Mod1.pin_25
  N43: R21.Pin_1, Mod1.pin_26

custom parts:
  Raspberry Pi Pico: Raspberry Pi Pico. Based around the RP2040 microcontroller the Pico is a low cost microcontroller device bringing Raspberry Pi quality, cost, and easy of use to the microcontroller space. Jan 2021, Split part in to two versions: tht (this one) and SMD. This one will drill holes for a .1 in header in pcb to allow plugging in the module as well as providing pads to solder the module to the top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
