# Fritzing sketch led_duell_schaltplan (saved by Fritzing 0.9.3b)
breadboards: 2

parts:
  LED10 = smd LED [color="Red (633nm)" package="0805 [SMD]"]
  LED16 = smd LED [color="Red (633nm)" package="0805 [SMD]"]
  LED8 = smd LED [color="Red (633nm)" package="0805 [SMD]"]
  LED21 = smd LED [color="Red (633nm)" package="0805 [SMD]"]
  LED9 = smd LED [color="Red (633nm)" package="0805 [SMD]"]
  LED17 = smd LED [color="Red (633nm)" package="0805 [SMD]"]
  LED7 = smd LED [color="Red (633nm)" package="0805 [SMD]"]
  LED5 = smd LED [color="Red (633nm)" package="0805 [SMD]"]
  LED1 = smd LED [color="Red (633nm)" package="0805 [SMD]"]
  LED14 = smd LED [color="Red (633nm)" package="0805 [SMD]"]
  LED3 = smd LED [color="Red (633nm)" package="0805 [SMD]"]
  LED12 = smd LED [color="Red (633nm)" package="0805 [SMD]"]
  LED19 = smd LED [color="Red (633nm)" package="0805 [SMD]"]
  LED2 = smd LED [color="Red (633nm)" package="0805 [SMD]"]
  LED15 = smd LED [color="Red (633nm)" package="0805 [SMD]"]
  LED11 = smd LED [color="Red (633nm)" package="0805 [SMD]"]
  LED4 = smd LED [color="Red (633nm)" package="0805 [SMD]"]
  LED13 = smd LED [color="Red (633nm)" package="0805 [SMD]"]
  LED18 = smd LED [color="Red (633nm)" package="0805 [SMD]"]
  LED20 = smd LED [color="Red (633nm)" package="0805 [SMD]"]
  LED6 = smd LED [color="Red (633nm)" package="0805 [SMD]"]
  R1 = Resistor [tolerance=±5% resistance=220 package=THT]
  R2 = Resistor [tolerance=±5% resistance=220 package=THT]
  R3 = Resistor [tolerance=±5% resistance=220 package=THT]
  R4 = Resistor [tolerance=±5% resistance=220 package=THT]
  R5 = Resistor [tolerance=±5% resistance=220 package=THT]
  R6 = Resistor [tolerance=±5% resistance=220 package=THT]
  R7 = Resistor [tolerance=±5% resistance=220 package=THT]
  R8 = Resistor [tolerance=±5% resistance=220 package=THT]
  R9 = Resistor [tolerance=±5% resistance=220 package=THT]
  R10 = Resistor [tolerance=±5% resistance=220 package=THT]
  R11 = Resistor [tolerance=±5% resistance=220 package=THT]
  R12 = Resistor [tolerance=±5% resistance=220 package=THT]
  R13 = Resistor [tolerance=±5% resistance=220 package=THT]
  R14 = Resistor [tolerance=±5% resistance=220 package=THT]
  R15 = Resistor [tolerance=±5% resistance=220 package=THT]
  R16 = Resistor [tolerance=±5% resistance=220 package=THT]
  R17 = Resistor [tolerance=±5% resistance=220 package=THT]
  R18 = Resistor [tolerance=±5% resistance=220 package=THT]
  R19 = Resistor [tolerance=±5% resistance=220 package=THT]
  R20 = Resistor [tolerance=±5% resistance=220 package=THT]
  R21 = Resistor [tolerance=±5% resistance=220 package=THT]
  PICO = Raspberry Pi Pico
  S1 = Pushbutton [package="[THT]"]
  S2 = Pushbutton [package="[THT]"]

nets:
  N1: LED10.cathode, R10.Pin_1
  N2: LED10.anode, PICO.pin_12
  N3: LED16.cathode, R16.Pin_1
  N4: LED16.anode, PICO.pin_20
  N5: LED8.cathode, R8.Pin_1
  N6: LED8.anode, PICO.pin_10
  N7: LED21.cathode, R21.Pin_0
  N8: LED21.anode, PICO.pin_26
  N9: LED9.cathode, R9.Pin_1
  N10: LED9.anode, PICO.pin_11
  N11: LED17.cathode, R17.Pin_0
  N12: LED17.anode, PICO.pin_21
  N13: LED7.cathode, R7.Pin_1
  N14: LED7.anode, PICO.pin_9
  N15: LED5.cathode, R5.Pin_1
  N16: LED5.anode, PICO.pin_6
  N17: LED1.cathode, R1.Pin_1
  N18: LED1.anode, PICO.pin_1
  N19: LED14.cathode, R14.Pin_1
  N20: LED14.anode, PICO.pin_17
  N21: LED3.cathode, R3.Pin_1
  N22: LED3.anode, PICO.pin_4
  N23: LED12.cathode, R12.Pin_1
  N24: LED12.anode, PICO.pin_15
  N25: LED19.cathode, R19.Pin_0
  N26: LED19.anode, PICO.pin_24
  N27: LED2.cathode, R2.Pin_1
  N28: LED2.anode, PICO.pin_2
  N29: LED15.cathode, R15.Pin_1
  N30: LED15.anode, PICO.pin_19
  N31: LED11.cathode, R11.Pin_1
  N32: LED11.anode, PICO.pin_14
  N33: LED4.cathode, R4.Pin_1
  N34: LED4.anode, PICO.pin_5
  N35: LED13.cathode, R13.Pin_1
  N36: LED13.anode, PICO.pin_16
  N37: LED18.cathode, R18.Pin_0
  N38: LED18.anode, PICO.pin_22
  N39: LED20.cathode, R20.Pin_0
  N40: LED20.anode, PICO.pin_25
  N41: LED6.cathode, R6.Pin_1
  N42: LED6.anode, PICO.pin_7
  GND: R1.Pin_0, R2.Pin_0, R3.Pin_0, R4.Pin_0, R5.Pin_0, R6.Pin_0, R7.Pin_0, R8.Pin_0, R9.Pin_0, R10.Pin_0, R11.Pin_0, R12.Pin_0, R13.Pin_0, R14.Pin_0, R15.Pin_0, R16.Pin_0, R17.Pin_1, R18.Pin_1, R19.Pin_1, R20.Pin_1, R21.Pin_1, PICO.pin_3, PICO.pin_8, PICO.pin_13, PICO.pin_18, PICO.pin_23, PICO.pin_28, PICO.pin_33, PICO.pin_38, S1.Pin_3, S1.Pin_4, S2.Pin_3, S2.Pin_4
  N43: PICO.pin_32, S1.Pin_1, S1.Pin_2
  N44: PICO.pin_34, S2.Pin_1, S2.Pin_2

custom parts:
  Raspberry Pi Pico: Raspberry Pi Pico. Based around the RP2040 microcontroller the Pico is a low cost microcontroller device bringing Raspberry Pi quality, cost, and easy of use to the microcontroller space. Jan 2021, Split part in to two versions: tht (this one) and SMD. This one will drill holes for a .1 in header in pcb to allow plugging in the module as well as providing pads to solder the module to the top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
